// Logisim project regbank.circ as structural Verilog: 1 circuit, main circuit regBank
module regBank (
  input  [7:0] regIn,
  input  inEn,
  input  [1:0] RegOut0Sel,
  input  [1:0] regInSel,
  input  [1:0] regOut1Sel,
  input  clk,
  input  reset,
  output [7:0] regOut0,
  output [7:0] regOut1
);

  wire decoder_1_out0, decoder_1_out1, decoder_1_out2, decoder_1_out3;
  wire [7:0] A_q, B_q, C_q, D_q;

  Decoder #(.select(2), .disabled(0)) decoder_1 (
    .out0(decoder_1_out0), .out1(decoder_1_out1), .out2(decoder_1_out2), .out3(decoder_1_out3),
    .sel(regInSel), .en(inEn));
  Register A (.D(regIn), .en(decoder_1_out0), .Q(A_q), .clk(clk), .clr(reset));
  Register B (.D(regIn), .en(decoder_1_out1), .Q(B_q), .clk(clk), .clr(reset));
  Register C (.D(regIn), .en(decoder_1_out2), .Q(C_q), .clk(clk), .clr(reset));
  Register D (.D(regIn), .en(decoder_1_out3), .Q(D_q), .clk(clk), .clr(reset));
  Multiplexer #(.select(2), .width(8), .enable("false")) multiplexer_1 (
    .in0(A_q), .in1(B_q), .in2(C_q), .in3(D_q), .out(regOut0), .sel(RegOut0Sel));
  Multiplexer #(.select(2), .width(8), .enable("false")) multiplexer_2 (
    .in0(A_q), .in1(B_q), .in2(C_q), .in3(D_q), .out(regOut1), .sel(regOut1Sel));
endmodule
