// Logisim project 4bitadderlab.circ as structural Verilog: 5 circuits, main circuit main
module main (
  input  [3:0] in_1,
  input  [3:0] in_2,
  input  in_3,
  output carry_out,
  output [3:0] out_5
);

  wire [3:0] G, P, Q;
  wire [3:1] carry;

  assign Q = in_1 ^ in_2;  // XOR_Gate xor_1, 4 bits wide
  assign P = in_1 | in_2;  // OR_Gate or_1, 4 bits wide
  assign G = in_1 & in_2;  // AND_Gate and_1, 4 bits wide
  k1 k1_1 (.P(in_1), .G(in_2), .k0(in_3), .k1(carry[1]));
  k2 k2_1 (.P(in_1), .G(in_2), .k0(in_3), .k2(carry[2]));
  k3 k3_1 (.P(in_1), .G(in_2), .k0(in_3), .k3(carry[3]));
  k4 k4_1 (.P(in_1), .G(in_2), .k0(in_3), .k4(carry_out));
  assign out_5 = {carry, in_3} ^ Q;  // XOR_Gate xor_2, 4 bits wide

  // Other names for the same wires on the sheet: carry[0] = in_3; k0 = in_3; X[3:0] = in_1; Y[3:0] = in_2
endmodule

module k1 (
  input  [3:0] P,
  input  [3:0] G,
  input  k0,
  output k1
);

  wire and_1_out;

  and and_1 (and_1_out, P[0], k0);
  or or_1 (k1, and_1_out, G[0]);
endmodule

module k2 (
  input  [3:0] P,
  input  [3:0] G,
  input  k0,
  output k2
);

  wire and_1_out, and_2_out;

  and and_1 (and_1_out, P[1], G[0]);
  and and_2 (and_2_out, P[0], P[1], k0);
  or or_1 (k2, and_1_out, G[1], and_2_out);
endmodule

module k3 (
  input  [3:0] P,
  input  [3:0] G,
  input  k0,
  output k3
);

  wire and_1_out, and_2_out, and_3_out;

  and and_1 (and_1_out, P[2], G[1]);
  and and_2 (and_2_out, P[2], P[1], G[0]);
  and and_3 (and_3_out, P[2], G[0], P[0], k0);
  or or_1 (k3, and_1_out, and_2_out, and_3_out, G[2]);
endmodule

module k4 (
  input  [3:0] P,
  input  [3:0] G,
  input  k0,
  output k4
);

  wire and_1_out, and_2_out, and_3_out, and_4_out;

  and and_1 (and_1_out, G[2], P[3]);
  and and_2 (and_2_out, P[3], P[2], G[1]);
  and and_3 (and_3_out, P[3], P[2], P[1], G[0]);
  and and_4 (and_4_out, P[3], P[2], P[1], P[0], k0);
  or or_1 (k4, and_1_out, and_4_out, and_2_out, and_3_out, G[3]);
endmodule
