// Logisim project memscanner.circ as structural Verilog: 2 circuits, main circuit main
module main (
  input  in_1,
  input  [7:0] in_2,
  input  in_3,
  input  in_4,
  input  sel,
  input  ld,
  input  clr,
  output [7:0] out_8
);

  wire clock_1_out;
  wire [7:0] A, D;

  count count_1 (.in_1({8{1'b0}}), .in_2(in_3), .out_3(A));
  Register register_1 (.D(D), .en(in_4), .Q(out_8), .clk(clock_1_out));  // open: clr
  Clock #(.highDuration(2), .lowDuration(2)) clock_1 (.out(clock_1_out));
  assign D = in_1 ? in_2 : 8'bz;  // Controlled_Buffer controlled_buffer_1
  RAM #(.bus("asynch")) ram_1 (.addr(A), .data(D), .sel(sel), .ld(ld), .clr(clr));
  Hex_Digit_Display hex_digit_display_1 (.value(out_8[7:4]), .dp(1'b1));
  Hex_Digit_Display hex_digit_display_2 (.value(out_8[3:0]), .dp(1'b1));
endmodule

module count (
  input  [7:0] in_1,
  input  in_2,
  output [7:0] out_3
);

  wire clock_1_out;
  wire [7:0] adder_1_out;

  Clock #(.highDuration(5), .lowDuration(5)) clock_1 (.out(clock_1_out));
  Adder adder_1 (.a(in_1), .b(out_3), .out(adder_1_out), .cin(1'b1));  // open: cout
  Register register_1 (.D(adder_1_out), .en(in_2), .Q(out_3), .clk(clock_1_out));  // open: clr
  Hex_Digit_Display hex_digit_display_1 (.value(out_3[7:4]), .dp(1'b0));
  Hex_Digit_Display hex_digit_display_2 (.value(out_3[3:0]), .dp(1'b0));
endmodule
