// Logisim project alu.circ as structural Verilog: 1 circuit, main circuit ALU
module ALU (
  input  [7:0] in1,
  input  [7:0] in2,
  input  ALUEn,
  input  [2:0] OpSel,
  input  [4:0] flagsIn,
  output [7:0] out_6,
  output [4:0] flagsOut
);

  wire and_1_out, and_2_out, and_3_out, and_4_out, B, C, or_2_out, or_3_out;
  wire [7:0] adder_1_out, and_5_out, demultiplexer_1_out0, demultiplexer_1_out1, demultiplexer_1_out2,
       demultiplexer_1_out3, demultiplexer_1_out4, demultiplexer_1_out5, demultiplexer_2_out0,
       demultiplexer_2_out1, demultiplexer_2_out2, demultiplexer_2_out4, demultiplexer_2_out5, not_1_out,
       or_1_out, shifter_1_out, subtractor_1_out;

  Demultiplexer #(.select(3), .width(8), .disabled(0)) demultiplexer_1 (
    .out0(demultiplexer_1_out0), .out1(demultiplexer_1_out1), .out2(demultiplexer_1_out2),
    .out3(demultiplexer_1_out3), .out4(demultiplexer_1_out4), .out5(demultiplexer_1_out5), .in(in1),
    .sel(OpSel), .en(ALUEn));  // open: out6, out7
  Demultiplexer #(.select(3), .width(8), .disabled(0)) demultiplexer_2 (
    .out0(demultiplexer_2_out0), .out1(demultiplexer_2_out1), .out2(demultiplexer_2_out2),
    .out4(demultiplexer_2_out4), .out5(demultiplexer_2_out5), .in(in2), .sel(OpSel), .en(ALUEn));  // open: out3, out6, out7
  and and_1 (and_1_out, ~in1[7], ~in2[7], flagsOut[2]);  // AND_Gate
  and and_2 (and_2_out, in1[7], in2[7], ~flagsOut[2]);  // AND_Gate
  and and_3 (and_3_out, ~in1[7], in2[7], flagsOut[2]);  // AND_Gate
  and and_4 (and_4_out, in1[7], ~in2[7], ~flagsOut[2]);  // AND_Gate
  Adder adder_1 (.a(demultiplexer_1_out0), .b(demultiplexer_2_out0), .out(adder_1_out), .cin(1'b0), .cout(C));
  Subtractor subtractor_1 (
    .a(demultiplexer_1_out1), .b(demultiplexer_2_out1), .out(subtractor_1_out), .bin(1'b0), .bout(B));
  Shifter #(.shift("lr")) shifter_1 (
    .in(demultiplexer_1_out2), .\dist (demultiplexer_2_out2[2:0]), .out(shifter_1_out));
  assign not_1_out = ~demultiplexer_1_out3;  // NOT_Gate not_1, 8 bits wide
  assign and_5_out = demultiplexer_1_out4 & demultiplexer_2_out4;  // AND_Gate and_5, 8 bits wide
  assign or_1_out = demultiplexer_1_out5 | demultiplexer_2_out5;  // OR_Gate or_1, 8 bits wide
  or or_2 (or_2_out, and_1_out, and_2_out);
  or or_3 (or_3_out, and_3_out, and_4_out);
  Multiplexer #(.select(3), .width(8)) multiplexer_1 (
    .in0(adder_1_out), .in1(subtractor_1_out), .in2(shifter_1_out), .in3(not_1_out), .in4(and_5_out),
    .in5(or_1_out), .out({flagsOut[2], out_6[6:0]}), .sel(OpSel), .en(ALUEn));  // open: in6, in7
  Multiplexer #(.select(3)) multiplexer_2 (
    .in0(or_2_out), .in1(or_3_out), .in2(flagsIn[3]), .in3(flagsIn[3]), .in4(flagsIn[3]), .in5(flagsIn[3]),
    .in6(flagsIn[3]), .in7(flagsIn[3]), .out(flagsOut[3]), .sel(OpSel), .en(ALUEn));
  Multiplexer #(.select(3)) multiplexer_3 (
    .in0(C), .in1(B), .in2(flagsIn[0]), .in3(flagsIn[0]), .in4(flagsIn[0]), .in5(flagsIn[0]),
    .in6(flagsIn[0]), .in7(flagsIn[0]), .out(flagsOut[0]), .sel(OpSel), .en(ALUEn));
  nor nor_1 (flagsOut[1], out_6[0], out_6[1], out_6[2], out_6[3], out_6[4], out_6[5], out_6[6], flagsOut[2]);
  xor xor_1 (flagsOut[4], flagsOut[3], flagsOut[2]);

  assign out_6[7] = flagsOut[2];

  // Other names for the same wires on the sheet: Cin = flagsIn[0]; Oin = flagsIn[3]; Cout = flagsOut[0];
  //   Zout = flagsOut[1]; Sout = flagsOut[2]; Oout = flagsOut[3]; S1 = in1[7]; S2 = in2[7]
endmodule
