// Logisim project 16bitripplecalc.circ as structural Verilog: 10 circuits, main circuit adder
module adder (
  input  Add_Sub,
  input  [7:0] Operand_X,
  input  [7:0] Operand_Y,
  input  in_4,
  output [7:0] Result,
  output carry_out
);

  wire [7:0] and_1_out, and_2_out, G, or_1_out, or_2_out, P, Q;
  wire [7:1] carry;

  LED #(.active("false")) Add_mode (.in(Add_Sub));
  k8 k8_1 (.P(Operand_X), .G(Operand_Y), .k0(in_4), .out_4(carry_out));
  LED Sub_mode (.in(Add_Sub));
  Hex_Digit_Display hex_digit_display_1 (.value(Operand_X[7:4]), .dp(1'b0));
  Hex_Digit_Display hex_digit_display_2 (.value(Operand_X[3:0]), .dp(1'b0));
  assign Q = Operand_X ^ Operand_Y;  // XOR_Gate xor_1, 8 bits wide
  assign or_1_out = Operand_X | Operand_Y;  // OR_Gate or_1, 8 bits wide
  assign and_1_out = Operand_X & Operand_Y;  // AND_Gate and_1, 8 bits wide
  assign and_2_out = ~Operand_X & Operand_Y;  // AND_Gate and_2, 8 bits wide
  assign or_2_out = ~Operand_X | Operand_Y;  // OR_Gate or_2, 8 bits wide
  Hex_Digit_Display hex_digit_display_3 (.value(Operand_Y[7:4]), .dp(1'b0));
  Multiplexer #(.width(8)) multiplexer_1 (.in0(or_1_out), .in1(or_2_out), .out(P), .sel(Add_Sub), .en(1'b1));
  Multiplexer #(.width(8)) multiplexer_2 (.in0(and_1_out), .in1(and_2_out), .out(G), .sel(Add_Sub), .en(1'b1));
  Hex_Digit_Display hex_digit_display_4 (.value(Operand_Y[3:0]), .dp(1'b0));
  Hex_Digit_Display hex_digit_display_5 (.value(Result[7:4]), .dp(1'b0));
  Hex_Digit_Display hex_digit_display_6 (.value(Result[3:0]), .dp(1'b0));
  assign Result = {carry, in_4} ^ Q;  // XOR_Gate xor_2, 8 bits wide
  k1 k1_1 (.P(P), .G(G), .k0(in_4), .k1(carry[1]));
  k2 k2_1 (.P(P), .G(G), .k0(in_4), .k2(carry[2]));
  k3 k3_1 (.P(P), .G(G), .k0(in_4), .k3(carry[3]));
  k4 k4_1 (.P(P), .G(G), .k0(in_4), .k4(carry[4]));
  k5 k5_1 (.P(P), .G(G), .k0(in_4), .k5(carry[5]));
  k6 k6_1 (.P(P), .G(G), .k0(in_4), .k5(carry[6]));
  k7 k7_1 (.P(P), .G(G), .k0(in_4), .k7(carry[7]));

  // Other names for the same wires on the sheet: as = Add_Sub; carry[0] = in_4; k0 = in_4; X[7:0] = Operand_X;
  //   Y[7:0] = Operand_Y

  // Notes on the sheet:
  //   Hex Display:
  //   +
  //   _
  //   =
endmodule

module k1 (
  input  [7:0] P,
  input  [7:0] G,
  input  k0,
  output k1
);

  wire and_1_out;

  and and_1 (and_1_out, P[0], k0);
  or or_1 (k1, and_1_out, G[0]);
endmodule

module k2 (
  input  [7:0] P,
  input  [7:0] G,
  input  k0,
  output k2
);

  wire and_1_out, and_2_out;

  and and_1 (and_1_out, P[1], G[0]);
  and and_2 (and_2_out, P[0], P[1], k0);
  or or_1 (k2, and_1_out, G[1], and_2_out);
endmodule

module k3 (
  input  [7:0] P,
  input  [7:0] G,
  input  k0,
  output k3
);

  wire and_1_out, and_2_out, and_3_out;

  and and_1 (and_1_out, P[2], G[1]);
  and and_2 (and_2_out, P[2], P[1], G[0]);
  and and_3 (and_3_out, P[2], G[0], P[0], k0);
  or or_1 (k3, and_1_out, and_2_out, and_3_out, G[2]);
endmodule

module k4 (
  input  [7:0] P,
  input  [7:0] G,
  input  k0,
  output k4
);

  wire and_1_out, and_2_out, and_3_out, and_4_out;

  and and_1 (and_1_out, G[2], P[3]);
  and and_2 (and_2_out, P[3], P[2], G[1]);
  and and_3 (and_3_out, P[3], P[2], P[1], G[0]);
  and and_4 (and_4_out, P[3], P[2], P[1], P[0], k0);
  or or_1 (k4, and_1_out, and_4_out, and_2_out, and_3_out, G[3]);
endmodule

module k5 (
  input  [7:0] P,
  input  [7:0] G,
  input  k0,
  output k5
);

  wire and_1_out, and_2_out, and_3_out, and_4_out, and_5_out;

  and and_1 (and_1_out, P[1], P[2], P[3], P[4], G[0]);
  and and_2 (and_2_out, 1'b1, P[2], P[4], G[1]);
  and and_3 (and_3_out, P[3], P[4], G[2]);
  and and_4 (and_4_out, P[4], G[3]);
  and and_5 (and_5_out, 1'b1, P[0], P[1], P[3], P[4], k0);
  or or_1 (k5, and_5_out, and_1_out, and_2_out, and_3_out, and_4_out, G[4]);

  // Other names for the same wires on the sheet: k5g0 = G[0]; k5g1 = G[1]; k5g2 = G[2]; k5g3 = G[3]; k5g4 = G[4];
  //   k5p0 = P[0]; k5p1 = P[1]; k5p2 = P[2]; k5p3 = P[3]; k5p4 = P[4]
endmodule

module k6 (
  input  [7:0] P,
  input  [7:0] G,
  input  k0,
  output k5
);

  wire and_1_out, and_2_out, and_3_out, and_4_out, and_5_out, and_6_out;

  and and_1 (and_1_out, P[0], P[1], P[2], P[3], P[4], P[5], k0);
  and and_2 (and_2_out, P[1], P[2], P[3], P[4], P[5], G[0]);
  and and_3 (and_3_out, P[2], P[3], P[4], P[5], G[1]);
  and and_4 (and_4_out, P[3], P[4], P[5], G[2]);
  or or_1 (k5, and_1_out, and_2_out, and_3_out, and_4_out, and_5_out, and_6_out, G[5]);
  and and_5 (and_5_out, P[4], P[5], G[3]);
  and and_6 (and_6_out, P[5], G[4]);

  // Other names for the same wires on the sheet: k6g0 = G[0]; k6g1 = G[1]; k6g2 = G[2]; k6g3 = G[3]; k6g4 = G[4];
  //   k6g5 = G[5]; k6p0 = P[0]; k6p1 = P[1]; k6p2 = P[2]; k6p3 = P[3]; k6p4 = P[4]; k6p5 = P[5]
endmodule

module k7 (
  input  [7:0] P,
  input  [7:0] G,
  input  k0,
  output k7
);

  wire and_1_out, and_2_out, and_3_out, and_4_out, and_5_out, and_6_out, and_7_out;

  and and_1 (and_1_out, P[0], P[1], P[2], P[3], P[4], P[5], P[6], k0);
  and and_2 (and_2_out, P[1], P[2], P[3], P[4], P[5], P[6], G[0]);
  or or_1 (k7, and_1_out, and_2_out, and_3_out, and_4_out, and_5_out, and_6_out, and_7_out, G[6]);
  and and_3 (and_3_out, P[2], P[3], P[4], P[5], P[6], G[1]);
  and and_4 (and_4_out, P[3], P[4], P[5], P[6], G[2]);
  and and_5 (and_5_out, P[4], P[5], P[6], G[3]);
  and and_6 (and_6_out, P[5], P[6], G[4]);
  and and_7 (and_7_out, P[6], G[5]);

  // Other names for the same wires on the sheet: k6g0 = G[0]; k6g1 = G[1]; k6g2 = G[2]; k6g3 = G[3]; k6g4 = G[4];
  //   k6g5 = G[5]; k6g6 = G[6]; k6p0 = P[0]; k6p1 = P[1]; k6p2 = P[2]; k6p3 = P[3]; k6p4 = P[4]; k6p5 = P[5];
  //   k6p6 = P[6]
endmodule

module k8 (
  input  [7:0] P,
  input  [7:0] G,
  input  k0,
  output out_4
);

  wire and_1_out, and_2_out, and_3_out, and_4_out, and_5_out, and_6_out, and_7_out, and_8_out;

  and and_1 (and_1_out, P[0], P[1], P[2], P[3], P[4], P[5], P[6], P[7], k0);
  and and_2 (and_2_out, P[1], P[2], P[3], P[4], P[6], P[7], G[0], P[5]);
  and and_3 (and_3_out, P[6], P[7], G[5]);
  and and_4 (and_4_out, P[2], P[3], P[4], P[5], P[6], P[7], G[1]);
  and and_5 (and_5_out, P[7], G[6]);
  and and_6 (and_6_out, P[5], P[6], G[4], P[7]);
  and and_7 (and_7_out, P[4], P[5], P[6], P[7], G[3]);
  or or_1 (out_4, G[7], and_3_out, and_5_out, and_6_out, and_7_out, and_1_out, and_2_out, and_4_out, and_8_out);
  and and_8 (and_8_out, P[3], P[4], P[5], P[7], G[2], P[6]);

  // Other names for the same wires on the sheet: k6g0 = G[0]; k6g1 = G[1]; k6g2 = G[2]; k6g3 = G[3]; k6g4 = G[4];
  //   k6g5 = G[5]; k6g6 = G[6]; k6g7 = G[7]; k6p0 = P[0]; k6p1 = P[1]; k6p2 = P[2]; k6p3 = P[3]; k6p4 = P[4];
  //   k6p5 = P[5]; k6p6 = P[6]; k6p7 = P[7]
endmodule

module main (
  input  Add_Sub_Toggle,
  input  [15:0] X_Operand,
  input  [15:0] Y_Operand,
  input  in_4,
  output [15:0] Result,
  output out_6
);

  wire adder_1_carry_out, multiplexer_1_out;

  Hex_Digit_Display hex_digit_display_1 (.value(X_Operand[15:12]), .dp(1'b0));
  LED #(.active("false")) Add_mode (.in(Add_Sub_Toggle));
  Hex_Digit_Display hex_digit_display_2 (.value(X_Operand[7:4]), .dp(1'b0));
  Hex_Digit_Display hex_digit_display_3 (.value(X_Operand[11:8]), .dp(1'b0));
  LED Sub_mode (.in(Add_Sub_Toggle));
  Hex_Digit_Display hex_digit_display_4 (.value(X_Operand[3:0]), .dp(1'b0));
  Hex_Digit_Display hex_digit_display_5 (.value(Y_Operand[11:8]), .dp(1'b0));
  Hex_Digit_Display hex_digit_display_6 (.value(Y_Operand[15:12]), .dp(1'b0));
  Hex_Digit_Display hex_digit_display_7 (.value(Y_Operand[3:0]), .dp(1'b0));
  Hex_Digit_Display hex_digit_display_8 (.value(Y_Operand[7:4]), .dp(1'b0));
  adder adder_1 (
    .Add_Sub(Add_Sub_Toggle), .Operand_X(X_Operand[7:0]), .Operand_Y(Y_Operand[7:0]), .in_4(in_4),
    .Result(Result[7:0]), .carry_out(adder_1_carry_out));
  adder adder_2 (
    .Add_Sub(Add_Sub_Toggle), .Operand_X(X_Operand[15:8]), .Operand_Y(Y_Operand[15:8]),
    .in_4(multiplexer_1_out), .Result(Result[15:8]), .carry_out(out_6));
  Multiplexer multiplexer_1 (
    .in0(adder_1_carry_out), .in1(in_4), .out(multiplexer_1_out), .sel(Add_Sub_Toggle), .en(1'b1));
  Hex_Digit_Display hex_digit_display_9 (.value(Result[15:12]), .dp(1'b0));
  Hex_Digit_Display hex_digit_display_10 (.value(Result[11:8]), .dp(1'b0));
  Hex_Digit_Display hex_digit_display_11 (.value(Result[3:0]), .dp(1'b0));
  Hex_Digit_Display hex_digit_display_12 (.value(Result[7:4]), .dp(1'b0));
  LED Carry_Flag (.in(out_6));

  // Other names for the same wires on the sheet: r11[3:0] = Result[11:8]; r15[3:0] = Result[15:12];
  //   as = Add_Sub_Toggle; cf = out_6; r3[3:0] = Result[3:0]; r7[3:0] = Result[7:4]; x3[3:0] = X_Operand[3:0];
  //   x7[3:0] = X_Operand[7:4]; x11[3:0] = X_Operand[11:8]; x15[3:0] = X_Operand[15:12]; y3[3:0] = Y_Operand[3:0];
  //   y7[3:0] = Y_Operand[7:4]; y11[3:0] = Y_Operand[11:8]; y15[3:0] = Y_Operand[15:12]

  // Notes on the sheet:
  //   _
  //   +
  //   =
endmodule
