// Logisim project 3-bit-carry-lookahead.circ as structural Verilog: 14 circuits, main circuit nand
module \nand  (
  input  in_1,
  input  in_2,
  output out_3
);

  wire transistor_3_out;

  Transistor transistor_1 (.in(1'b1), .out(out_3), .gate(in_1));
  Transistor #(.\type ("n")) transistor_2 (.in(transistor_3_out), .out(out_3), .gate(in_1));
  Transistor #(.\type ("n")) transistor_3 (.in(1'b0), .out(transistor_3_out), .gate(in_2));
  Transistor #(.gate("br")) transistor_4 (.in(1'b1), .out(out_3), .gate(in_2));
endmodule

module \not  (
  input  in_1,
  output out_2
);

  \nand  nand_1 (.in_1(in_1), .in_2(in_1), .out_3(out_2));
endmodule

module \and  (
  input  in_1,
  input  in_2,
  output out_3
);

  wire nand_1_out_3;

  \nand  nand_1 (.in_1(in_1), .in_2(in_2), .out_3(nand_1_out_3));
  \nand  nand_2 (.in_1(nand_1_out_3), .in_2(nand_1_out_3), .out_3(out_3));
endmodule

module \or  (
  input  in_1,
  input  in_2,
  output out_3
);

  wire nand_1_out_3, nand_2_out_3;

  \nand  nand_1 (.in_1(in_1), .in_2(in_1), .out_3(nand_1_out_3));
  \nand  nand_2 (.in_1(in_2), .in_2(in_2), .out_3(nand_2_out_3));
  \nand  nand_3 (.in_1(nand_1_out_3), .in_2(nand_2_out_3), .out_3(out_3));
endmodule

module cond (
  input  in_1,
  input  in_2,
  output out_3
);

  wire not_1_out_2;

  \not  not_1 (.in_1(in_1), .out_2(not_1_out_2));
  \or  or_1 (.in_1(not_1_out_2), .in_2(in_2), .out_3(out_3));
endmodule

module \xor  (
  input  in_1,
  input  in_2,
  output out_3
);

  wire and_1_out_3, not_1_out_2, or_1_out_3;

  \or  or_1 (.in_1(in_1), .in_2(in_2), .out_3(or_1_out_3));
  \and  and_1 (.in_1(in_1), .in_2(in_2), .out_3(and_1_out_3));
  \not  not_1 (.in_1(and_1_out_3), .out_2(not_1_out_2));
  \and  and_2 (.in_1(or_1_out_3), .in_2(not_1_out_2), .out_3(out_3));
endmodule

module biconditional (
  input  in_1,
  input  in_2,
  output out_3
);

  wire cond_1_out_3, cond_2_out_3;

  cond cond_1 (.in_1(in_1), .in_2(in_2), .out_3(cond_1_out_3));
  cond cond_2 (.in_1(in_2), .in_2(in_1), .out_3(cond_2_out_3));
  \and  and_1 (.in_1(cond_1_out_3), .in_2(cond_2_out_3), .out_3(out_3));
endmodule

module P_i (
  input  in_1,
  input  in_2,
  output out_3
);

  \or  or_1 (.in_1(in_1), .in_2(in_2), .out_3(out_3));
endmodule

module G_i (
  input  in_1,
  input  in_2,
  output out_3
);

  \and  and_1 (.in_1(in_1), .in_2(in_2), .out_3(out_3));
endmodule

module R_x_y (
  input  in_1,
  input  in_2,
  output out_3
);

  \xor  xor_1 (.in_1(in_1), .in_2(in_2), .out_3(out_3));
endmodule

module _3_bit_cl (
  input  X_Operand,
  input  in_2,
  input  C_i,
  input  in_4,
  input  Y_Operand,
  input  in_6,
  input  in_7,
  output C_o,
  output out_9,
  output Sum,
  output out_11
);

  wire k_1_1_k, k_2_1_k_2, r_x_y_1_out_3, r_x_y_2_out_3, r_x_y_5_out_3;

  R_x_y r_x_y_1 (.in_1(X_Operand), .in_2(Y_Operand), .out_3(r_x_y_1_out_3));
  R_x_y r_x_y_2 (.in_1(in_2), .in_2(in_6), .out_3(r_x_y_2_out_3));
  R_x_y r_x_y_3 (.in_1(r_x_y_1_out_3), .in_2(k_2_1_k_2), .out_3(out_9));
  R_x_y r_x_y_4 (.in_1(r_x_y_2_out_3), .in_2(k_1_1_k), .out_3(Sum));
  R_x_y r_x_y_5 (.in_1(C_i), .in_2(in_7), .out_3(r_x_y_5_out_3));
  R_x_y r_x_y_6 (.in_1(r_x_y_5_out_3), .in_2(in_4), .out_3(out_11));
  K_1 k_1_1 (.x(C_i), .y(in_7), .c(in_4), .k(k_1_1_k));
  K_2 k_2_1 (.X_0(C_i), .Y_0(in_7), .X_1(in_2), .Y_1(in_6), .C(in_4), .K_2(k_2_1_k_2));
  K_3 k_3_1 (.X_0(C_i), .Y_0(in_7), .X_1(in_2), .Y_1(in_6), .X_2(X_Operand), .Y_2(Y_Operand), .c(in_4), .K_3(C_o));

  // Notes on the sheet:
  //   MSB on left
  //   LSB on right
endmodule

module K_1 (
  input  x,
  input  y,
  input  c,
  output k
);

  wire and_1_out_3, g_i_1_out_3, p_i_1_out_3;

  G_i g_i_1 (.in_1(x), .in_2(y), .out_3(g_i_1_out_3));
  P_i p_i_1 (.in_1(x), .in_2(x), .out_3(p_i_1_out_3));
  \and  and_1 (.in_1(p_i_1_out_3), .in_2(c), .out_3(and_1_out_3));
  \or  or_1 (.in_1(g_i_1_out_3), .in_2(and_1_out_3), .out_3(k));
endmodule

module K_2 (
  input  X_0,
  input  Y_0,
  input  X_1,
  input  Y_1,
  input  C,
  output K_2
);

  wire and_1_out_3, and_2_out_3, and_3_out_3, g_i_1_out_3, g_i_2_out_3, or_1_out_3, p_i_1_out_3, p_i_2_out_3;

  G_i g_i_1 (.in_1(X_0), .in_2(Y_0), .out_3(g_i_1_out_3));
  P_i p_i_1 (.in_1(X_0), .in_2(Y_0), .out_3(p_i_1_out_3));
  G_i g_i_2 (.in_1(X_1), .in_2(Y_1), .out_3(g_i_2_out_3));
  P_i p_i_2 (.in_1(X_1), .in_2(Y_1), .out_3(p_i_2_out_3));
  \and  and_1 (.in_1(g_i_1_out_3), .in_2(p_i_2_out_3), .out_3(and_1_out_3));
  \and  and_2 (.in_1(p_i_2_out_3), .in_2(p_i_1_out_3), .out_3(and_2_out_3));
  \and  and_3 (.in_1(and_2_out_3), .in_2(C), .out_3(and_3_out_3));
  \or  or_1 (.in_1(and_1_out_3), .in_2(and_3_out_3), .out_3(or_1_out_3));
  \or  or_2 (.in_1(g_i_2_out_3), .in_2(or_1_out_3), .out_3(K_2));
endmodule

module K_3 (
  input  X_0,
  input  Y_0,
  input  X_1,
  input  Y_1,
  input  X_2,
  input  Y_2,
  input  c,
  output K_3
);

  wire and_1_out_3, and_2_out_3, and_3_out_3, and_4_out_3, and_5_out_3, and_6_out_3, g_i_1_out_3,
       g_i_2_out_3, g_i_3_out_3, or_1_out_3, or_2_out_3, p_i_1_out_3, p_i_2_out_3, p_i_3_out_3;

  G_i g_i_1 (.in_1(X_0), .in_2(Y_0), .out_3(g_i_1_out_3));
  P_i p_i_1 (.in_1(X_0), .in_2(Y_0), .out_3(p_i_1_out_3));
  G_i g_i_2 (.in_1(X_1), .in_2(Y_1), .out_3(g_i_2_out_3));
  P_i p_i_2 (.in_1(X_1), .in_2(Y_1), .out_3(p_i_2_out_3));
  G_i g_i_3 (.in_1(X_2), .in_2(Y_2), .out_3(g_i_3_out_3));
  P_i p_i_3 (.in_1(X_2), .in_2(Y_2), .out_3(p_i_3_out_3));
  \and  and_1 (.in_1(g_i_2_out_3), .in_2(p_i_3_out_3), .out_3(and_1_out_3));
  \and  and_2 (.in_1(p_i_2_out_3), .in_2(p_i_3_out_3), .out_3(and_2_out_3));
  \and  and_3 (.in_1(g_i_1_out_3), .in_2(and_2_out_3), .out_3(and_3_out_3));
  \and  and_4 (.in_1(c), .in_2(p_i_1_out_3), .out_3(and_4_out_3));
  \and  and_5 (.in_1(p_i_2_out_3), .in_2(p_i_3_out_3), .out_3(and_5_out_3));
  \and  and_6 (.in_1(and_4_out_3), .in_2(and_5_out_3), .out_3(and_6_out_3));
  \or  or_1 (.in_1(and_3_out_3), .in_2(and_1_out_3), .out_3(or_1_out_3));
  \or  or_2 (.in_1(and_6_out_3), .in_2(g_i_3_out_3), .out_3(or_2_out_3));
  \or  or_3 (.in_1(or_1_out_3), .in_2(or_2_out_3), .out_3(K_3));
endmodule
