// Logisim project 3bitaddsublab.circ as structural Verilog: 4 circuits, main circuit main
module main (
  input  [2:0] in_1,
  input  [2:0] in_2,
  input  in_3,
  input  a_s,
  output [2:0] out_5,
  output carry_borrow_out
);

  wire [2:0] G, P, Q, xnor_1_out;
  wire [2:1] carry;

  assign Q = in_1 ^ in_2;  // XOR_Gate xor_1, 3 bits wide
  assign P = xnor_1_out | in_2;  // OR_Gate or_1, 3 bits wide
  assign G = xnor_1_out & in_2;  // AND_Gate and_1, 3 bits wide
  assign xnor_1_out = ~(in_1 ^ {3{a_s}});  // XNOR_Gate xnor_1, 3 bits wide
  k1 k1_1 (.P(P), .G(G), .k0(in_3), .k1(carry[1]));
  k2 k2_1 (.P(P), .G(G), .k0(in_3), .k2(carry[2]));
  k3 k3_1 (.P(P), .G(G), .k0(in_3), .k3(carry_borrow_out));
  assign out_5 = {carry, in_3} ^ Q;  // XOR_Gate xor_2, 3 bits wide

  // Other names for the same wires on the sheet: addsub = a_s; carry[0] = in_3; k0 = in_3; X[2:0] = in_1;
  //   Y[2:0] = in_2

  // Notes on the sheet:
  //   3 Bit Adder Subtractor
endmodule

module k1 (
  input  [2:0] P,
  input  [2:0] G,
  input  k0,
  output k1
);

  wire and_1_out;

  and and_1 (and_1_out, P[0], k0);
  or or_1 (k1, and_1_out, G[0]);
endmodule

module k2 (
  input  [2:0] P,
  input  [2:0] G,
  input  k0,
  output k2
);

  wire and_1_out, and_2_out;

  and and_1 (and_1_out, P[1], G[0]);
  and and_2 (and_2_out, P[0], P[1], k0);
  or or_1 (k2, and_1_out, G[1], and_2_out);
endmodule

module k3 (
  input  [2:0] P,
  input  [2:0] G,
  input  k0,
  output k3
);

  wire and_1_out, and_2_out, and_3_out;

  and and_1 (and_1_out, P[2], G[1]);
  and and_2 (and_2_out, P[2], P[1], G[0]);
  and and_3 (and_3_out, P[2], G[0], P[0], k0);
  or or_1 (k3, and_1_out, and_2_out, and_3_out, G[2]);
endmodule
