// Logisim project 8bitaddsub_final_feb16.circ as structural Verilog: 11 circuits, main circuit 8bitaddsubcmp
module _8bitaddsubcmp (
  input  Add_Sub,
  input  [7:0] Operand_X,
  input  [7:0] Operand_Y,
  input  in_4,
  output [7:0] Result,
  output OA_Flag,
  output L_flag,
  output carry_borrow_out,
  output O_flag
);

  wire [7:0] G, P, Q, xnor_1_out;
  wire [7:1] carry;

  OA oa_1 (.x(Operand_X), .y(Operand_Y), .d(Result), .out(OA_Flag));
  k8 k8_1 (.P(Operand_X), .G(Operand_Y), .k0(in_4), .out_4(carry_borrow_out));
  LED Add_mode (.in(Add_Sub));
  LED #(.active("false")) Sub_mode (.in(Add_Sub));
  Hex_Digit_Display hex_digit_display_1 (.value(Operand_X[3:0]), .dp(1'b0));
  Hex_Digit_Display hex_digit_display_2 (.value(Operand_X[7:4]), .dp(1'b0));
  assign Q = Operand_X ^ Operand_Y;  // XOR_Gate xor_1, 8 bits wide
  assign xnor_1_out = ~(Operand_X ^ {8{Add_Sub}});  // XNOR_Gate xnor_1, 8 bits wide
  assign P = xnor_1_out | Operand_Y;  // OR_Gate or_1, 8 bits wide
  assign G = xnor_1_out & Operand_Y;  // AND_Gate and_1, 8 bits wide
  Hex_Digit_Display hex_digit_display_3 (.value(Operand_Y[7:4]), .dp(1'b0));
  O o_1 (.x(Operand_X), .y(Operand_Y), .d(Result), .out(O_flag));
  Hex_Digit_Display hex_digit_display_4 (.value(Operand_Y[3:0]), .dp(1'b0));
  xor xor_2 (L_flag, Result[7], O_flag);
  Hex_Digit_Display hex_digit_display_5 (.value(Result[7:4]), .dp(1'b0));
  Hex_Digit_Display hex_digit_display_6 (.value(Result[3:0]), .dp(1'b0));
  assign Result = {carry, in_4} ^ Q;  // XOR_Gate xor_3, 8 bits wide
  k1 k1_1 (.P(P), .G(G), .k0(in_4), .k1(carry[1]));
  k2 k2_1 (.P(P), .G(G), .k0(in_4), .k2(carry[2]));
  k3 k3_1 (.P(P), .G(G), .k0(in_4), .k3(carry[3]));
  k4 k4_1 (.P(P), .G(G), .k0(in_4), .k4(carry[4]));
  k5 k5_1 (.P(P), .G(G), .k0(in_4), .k5(carry[5]));
  k6 k6_1 (.P(P), .G(G), .k0(in_4), .k5(carry[6]));
  k7 k7_1 (.P(P), .G(G), .k0(in_4), .k7(carry[7]));

  // Other names for the same wires on the sheet: as = Add_Sub; carry[0] = in_4; k0 = in_4; D[7:0] = Result;
  //   X[7:0] = Operand_X; Y[7:0] = Operand_Y

  // Notes on the sheet:
  //   Hex Display:
  //   A carry out indicates overflow
  //   for unsigned numbers
  //   A borrow out indicates x<y for 
  //   unsigned numbers
  //   The OA flag indicates overflow
  //   for signed addition in add mode
  //   +
  //   _
  //   The L flag indicates x<y
  //   for signed numbers in sub mode
  //   The O flag indicates overflow
  //   for signed subtraction in sub mode
  //   =
endmodule

module k1 (
  input  [7:0] P,
  input  [7:0] G,
  input  k0,
  output k1
);

  wire and_1_out;

  and and_1 (and_1_out, P[0], k0);
  or or_1 (k1, and_1_out, G[0]);
endmodule

module k2 (
  input  [7:0] P,
  input  [7:0] G,
  input  k0,
  output k2
);

  wire and_1_out, and_2_out;

  and and_1 (and_1_out, P[1], G[0]);
  and and_2 (and_2_out, P[0], P[1], k0);
  or or_1 (k2, and_1_out, G[1], and_2_out);
endmodule

module k3 (
  input  [7:0] P,
  input  [7:0] G,
  input  k0,
  output k3
);

  wire and_1_out, and_2_out, and_3_out;

  and and_1 (and_1_out, P[2], G[1]);
  and and_2 (and_2_out, P[2], P[1], G[0]);
  and and_3 (and_3_out, P[2], G[0], P[0], k0);
  or or_1 (k3, and_1_out, and_2_out, and_3_out, G[2]);
endmodule

module k4 (
  input  [7:0] P,
  input  [7:0] G,
  input  k0,
  output k4
);

  wire and_1_out, and_2_out, and_3_out, and_4_out;

  and and_1 (and_1_out, G[2], P[3]);
  and and_2 (and_2_out, P[3], P[2], G[1]);
  and and_3 (and_3_out, P[3], P[2], P[1], G[0]);
  and and_4 (and_4_out, P[3], P[2], P[1], P[0], k0);
  or or_1 (k4, and_1_out, and_4_out, and_2_out, and_3_out, G[3]);
endmodule

module k5 (
  input  [7:0] P,
  input  [7:0] G,
  input  k0,
  output k5
);

  wire and_1_out, and_2_out, and_3_out, and_4_out, and_5_out;

  and and_1 (and_1_out, P[1], P[2], P[3], P[4], G[0]);
  and and_2 (and_2_out, 1'b1, P[2], P[4], G[1]);
  and and_3 (and_3_out, P[3], P[4], G[2]);
  and and_4 (and_4_out, P[4], G[3]);
  and and_5 (and_5_out, 1'b1, P[0], P[1], P[3], P[4], k0);
  or or_1 (k5, and_5_out, and_1_out, and_2_out, and_3_out, and_4_out, G[4]);

  // Other names for the same wires on the sheet: k5g0 = G[0]; k5g1 = G[1]; k5g2 = G[2]; k5g3 = G[3]; k5g4 = G[4];
  //   k5p0 = P[0]; k5p1 = P[1]; k5p2 = P[2]; k5p3 = P[3]; k5p4 = P[4]
endmodule

module k6 (
  input  [7:0] P,
  input  [7:0] G,
  input  k0,
  output k5
);

  wire and_1_out, and_2_out, and_3_out, and_4_out, and_5_out, and_6_out;

  and and_1 (and_1_out, P[0], P[1], P[2], P[3], P[4], P[5], k0);
  and and_2 (and_2_out, P[1], P[2], P[3], P[4], P[5], G[0]);
  and and_3 (and_3_out, P[2], P[3], P[4], P[5], G[1]);
  and and_4 (and_4_out, P[3], P[4], P[5], G[2]);
  or or_1 (k5, and_1_out, and_2_out, and_3_out, and_4_out, and_5_out, and_6_out, G[5]);
  and and_5 (and_5_out, P[4], P[5], G[3]);
  and and_6 (and_6_out, P[5], G[4]);

  // Other names for the same wires on the sheet: k6g0 = G[0]; k6g1 = G[1]; k6g2 = G[2]; k6g3 = G[3]; k6g4 = G[4];
  //   k6g5 = G[5]; k6p0 = P[0]; k6p1 = P[1]; k6p2 = P[2]; k6p3 = P[3]; k6p4 = P[4]; k6p5 = P[5]
endmodule

module k7 (
  input  [7:0] P,
  input  [7:0] G,
  input  k0,
  output k7
);

  wire and_1_out, and_2_out, and_3_out, and_4_out, and_5_out, and_6_out, and_7_out;

  and and_1 (and_1_out, P[0], P[1], P[2], P[3], P[4], P[5], P[6], k0);
  and and_2 (and_2_out, P[1], P[2], P[3], P[4], P[5], P[6], G[0]);
  or or_1 (k7, and_1_out, and_2_out, and_3_out, and_4_out, and_5_out, and_6_out, and_7_out, G[6]);
  and and_3 (and_3_out, P[2], P[3], P[4], P[5], P[6], G[1]);
  and and_4 (and_4_out, P[3], P[4], P[5], P[6], G[2]);
  and and_5 (and_5_out, P[4], P[5], P[6], G[3]);
  and and_6 (and_6_out, P[5], P[6], G[4]);
  and and_7 (and_7_out, P[6], G[5]);

  // Other names for the same wires on the sheet: k6g0 = G[0]; k6g1 = G[1]; k6g2 = G[2]; k6g3 = G[3]; k6g4 = G[4];
  //   k6g5 = G[5]; k6g6 = G[6]; k6p0 = P[0]; k6p1 = P[1]; k6p2 = P[2]; k6p3 = P[3]; k6p4 = P[4]; k6p5 = P[5];
  //   k6p6 = P[6]
endmodule

module k8 (
  input  [7:0] P,
  input  [7:0] G,
  input  k0,
  output out_4
);

  wire and_1_out, and_2_out, and_3_out, and_4_out, and_5_out, and_6_out, and_7_out, and_8_out;

  and and_1 (and_1_out, P[0], P[1], P[2], P[3], P[4], P[5], P[6], P[7], k0);
  and and_2 (and_2_out, P[1], P[2], P[3], P[4], P[6], P[7], G[0], P[5]);
  and and_3 (and_3_out, P[6], P[7], G[5]);
  and and_4 (and_4_out, P[2], P[3], P[4], P[5], P[6], P[7], G[1]);
  and and_5 (and_5_out, P[7], G[6]);
  and and_6 (and_6_out, P[5], P[6], G[4], P[7]);
  and and_7 (and_7_out, P[4], P[5], P[6], P[7], G[3]);
  or or_1 (out_4, G[7], and_3_out, and_5_out, and_6_out, and_7_out, and_1_out, and_2_out, and_4_out, and_8_out);
  and and_8 (and_8_out, P[3], P[4], P[5], P[7], G[2], P[6]);

  // Other names for the same wires on the sheet: k6g0 = G[0]; k6g1 = G[1]; k6g2 = G[2]; k6g3 = G[3]; k6g4 = G[4];
  //   k6g5 = G[5]; k6g6 = G[6]; k6g7 = G[7]; k6p0 = P[0]; k6p1 = P[1]; k6p2 = P[2]; k6p3 = P[3]; k6p4 = P[4];
  //   k6p5 = P[5]; k6p6 = P[6]; k6p7 = P[7]
endmodule

module O (
  input  [7:0] x,
  input  [7:0] y,
  input  [7:0] d,
  output out
);

  wire and_1_out, and_2_out;

  and and_1 (and_1_out, x[7], ~y[7], ~d[7]);  // AND_Gate
  or or_1 (out, and_1_out, and_2_out);
  and and_2 (and_2_out, ~x[7], y[7], d[7]);  // AND_Gate
endmodule

module OA (
  input  [7:0] x,
  input  [7:0] y,
  input  [7:0] d,
  output out
);

  wire and_1_out, and_2_out;

  and and_1 (and_1_out, ~x[7], ~y[7], d[7]);  // AND_Gate
  or or_1 (out, and_1_out, and_2_out);
  and and_2 (and_2_out, x[7], y[7], ~d[7]);  // AND_Gate
endmodule
