// Logisim project fixedcl.circ as structural Verilog: 17 circuits, main circuit nand
module \nand  (
  input  in_1,
  input  in_2,
  output out_3
);

  wire transistor_3_out;

  Transistor transistor_1 (.in(1'b1), .out(out_3), .gate(in_1));
  Transistor #(.\type ("n")) transistor_2 (.in(transistor_3_out), .out(out_3), .gate(in_1));
  Transistor #(.\type ("n")) transistor_3 (.in(1'b0), .out(transistor_3_out), .gate(in_2));
  Transistor #(.gate("br")) transistor_4 (.in(1'b1), .out(out_3), .gate(in_2));
endmodule

module \not  (
  input  in_1,
  output out_2
);

  \nand  nand_1 (.in_1(in_1), .in_2(in_1), .out_3(out_2));
endmodule

module \and  (
  input  in_1,
  input  in_2,
  output out_3
);

  wire nand_1_out_3;

  \nand  nand_1 (.in_1(in_1), .in_2(in_2), .out_3(nand_1_out_3));
  \nand  nand_2 (.in_1(nand_1_out_3), .in_2(nand_1_out_3), .out_3(out_3));
endmodule

module \or  (
  input  in_1,
  input  in_2,
  output out_3
);

  wire nand_1_out_3, nand_2_out_3;

  \nand  nand_1 (.in_1(in_1), .in_2(in_1), .out_3(nand_1_out_3));
  \nand  nand_2 (.in_1(in_2), .in_2(in_2), .out_3(nand_2_out_3));
  \nand  nand_3 (.in_1(nand_1_out_3), .in_2(nand_2_out_3), .out_3(out_3));
endmodule

module cond (
  input  in_1,
  input  in_2,
  output out_3
);

  wire not_1_out_2;

  \not  not_1 (.in_1(in_1), .out_2(not_1_out_2));
  \or  or_1 (.in_1(not_1_out_2), .in_2(in_2), .out_3(out_3));
endmodule

module \xor  (
  input  in_1,
  input  in_2,
  output out_3
);

  wire and_1_out_3, not_1_out_2, or_1_out_3;

  \or  or_1 (.in_1(in_1), .in_2(in_2), .out_3(or_1_out_3));
  \and  and_1 (.in_1(in_1), .in_2(in_2), .out_3(and_1_out_3));
  \not  not_1 (.in_1(and_1_out_3), .out_2(not_1_out_2));
  \and  and_2 (.in_1(or_1_out_3), .in_2(not_1_out_2), .out_3(out_3));
endmodule

module biconditional (
  input  in_1,
  input  in_2,
  output out_3
);

  wire cond_1_out_3, cond_2_out_3;

  cond cond_1 (.in_1(in_1), .in_2(in_2), .out_3(cond_1_out_3));
  cond cond_2 (.in_1(in_2), .in_2(in_1), .out_3(cond_2_out_3));
  \and  and_1 (.in_1(cond_1_out_3), .in_2(cond_2_out_3), .out_3(out_3));
endmodule

module half_adder (
  input  x,
  input  y,
  output r,
  output carry
);

  wire and_1_out_3, and_2_out_3, not_1_out_2, not_2_out_2;

  \and  and_1 (.in_1(x), .in_2(not_1_out_2), .out_3(and_1_out_3));
  \not  not_1 (.in_1(y), .out_2(not_1_out_2));
  \not  not_2 (.in_1(x), .out_2(not_2_out_2));
  \and  and_2 (.in_1(not_2_out_2), .in_2(y), .out_3(and_2_out_3));
  \and  and_3 (.in_1(x), .in_2(y), .out_3(carry));
  \or  or_1 (.in_1(and_1_out_3), .in_2(and_2_out_3), .out_3(r));
endmodule

module full_adder (
  input  x,
  input  y,
  input  carry_in,
  output sum,
  output carry_out
);

  wire half_adder_1_carry, half_adder_1_r, half_adder_2_carry;

  half_adder half_adder_1 (.x(x), .y(y), .r(half_adder_1_r), .carry(half_adder_1_carry));
  half_adder half_adder_2 (.x(half_adder_1_r), .y(carry_in), .r(sum), .carry(half_adder_2_carry));
  \or  or_1 (.in_1(half_adder_1_carry), .in_2(half_adder_2_carry), .out_3(carry_out));
endmodule

module _3bit_adder (
  input  Operand_A_Bits,
  input  in_2,
  input  in_3,
  input  c_i,
  input  in_5,
  input  Operand_B_Bits,
  input  in_7,
  output out_8,
  output Result_Bits,
  output out_10,
  output c_o
);

  wire full_adder_1_carry_out, full_adder_2_carry_out;

  full_adder full_adder_1 (.x(in_3), .y(in_7), .carry_in(c_i), .sum(out_10), .carry_out(full_adder_1_carry_out));
  full_adder full_adder_2 (
    .x(in_2), .y(Operand_B_Bits), .carry_in(full_adder_1_carry_out), .sum(Result_Bits),
    .carry_out(full_adder_2_carry_out));
  full_adder full_adder_3 (
    .x(Operand_A_Bits), .y(in_5), .carry_in(full_adder_2_carry_out), .sum(out_8), .carry_out(c_o));

  // Notes on the sheet:
  //   MSB on left
endmodule

module carry_look_ahead (
  input  in_1,
  input  y,
  input  in_3,
  output r,
  output c_o
);

  wire and_1_out_3, and_2_out_3, and_3_out_3, and_4_out_3, not_1_out_2, not_2_out_2, or_1_out_3;

  \and  and_1 (.in_1(in_1), .in_2(y), .out_3(and_1_out_3));
  \or  or_1 (.in_1(in_1), .in_2(in_1), .out_3(or_1_out_3));
  \and  and_2 (.in_1(in_1), .in_2(not_1_out_2), .out_3(and_2_out_3));
  \not  not_1 (.in_1(y), .out_2(not_1_out_2));
  \and  and_3 (.in_1(not_2_out_2), .in_2(y), .out_3(and_3_out_3));
  \not  not_2 (.in_1(in_1), .out_2(not_2_out_2));
  \and  and_4 (.in_1(or_1_out_3), .in_2(in_3), .out_3(and_4_out_3));
  \or  or_2 (.in_1(and_2_out_3), .in_2(and_3_out_3), .out_3(r));
  \or  or_3 (.in_1(and_1_out_3), .in_2(and_4_out_3), .out_3(c_o));
endmodule

module _3bit_cl (
  input  in_1,
  input  in_2,
  input  Operand_A,
  input  Operand_B,
  input  in_5,
  input  in_6,
  input  c_i,
  output Sum,
  output out_9,
  output out_10,
  output c_o
);

  carry_look_ahead carry_look_ahead_1 (.in_1(Operand_A), .y(in_6), .in_3(c_i), .r(out_10));  // open: c_o
  carry_look_ahead carry_look_ahead_2 (.in_1(in_2), .y(in_5), .in_3(c_i), .r(out_9));  // open: c_o
  carry_look_ahead carry_look_ahead_3 (.in_1(Operand_B), .y(in_1), .in_3(c_i), .r(Sum), .c_o(c_o));

  // Notes on the sheet:
  //   MSB on left
endmodule

module g (
  input  in_1,
  input  in_2,
  output out_3
);

  wire nand_1_out_3;

  \nand  nand_1 (.in_1(in_1), .in_2(in_2), .out_3(nand_1_out_3));
  \nand  nand_2 (.in_1(nand_1_out_3), .in_2(nand_1_out_3), .out_3(out_3));
endmodule

module p (
  input  in_1,
  input  in_2,
  output out_3
);

  wire nand_1_out_3, nand_2_out_3;

  \nand  nand_1 (.in_1(in_1), .in_2(in_1), .out_3(nand_1_out_3));
  \nand  nand_2 (.in_1(in_2), .in_2(in_2), .out_3(nand_2_out_3));
  \nand  nand_3 (.in_1(nand_1_out_3), .in_2(nand_2_out_3), .out_3(out_3));
endmodule

module k0 (
  input  in_1,
  input  in_2,
  input  in_3,
  output out_4,
  output out_5
);

  wire and_1_out_3, and_2_out_3, not_1_out_2, not_2_out_2;

  \not  not_1 (.in_1(in_2), .out_2(not_1_out_2));
  \and  and_1 (.in_1(in_1), .in_2(not_1_out_2), .out_3(and_1_out_3));
  \not  not_2 (.in_1(in_1), .out_2(not_2_out_2));
  \and  and_2 (.in_1(not_2_out_2), .in_2(in_2), .out_3(and_2_out_3));
  \or  or_1 (.in_1(and_1_out_3), .in_2(and_2_out_3), .out_3(out_4));

  assign out_5 = in_3;
endmodule

module k1 (
  input  in_1,
  input  in_2,
  input  in_3,
  output out_4,
  output out_5
);

  wire and_1_out_3, and_2_out_3, and_3_out_3, g_1_out_3, not_1_out_2, not_2_out_2, p_1_out_3;

  \not  not_1 (.in_1(in_2), .out_2(not_1_out_2));
  \and  and_1 (.in_1(in_1), .in_2(not_1_out_2), .out_3(and_1_out_3));
  \and  and_2 (.in_1(not_2_out_2), .in_2(in_2), .out_3(and_2_out_3));
  \not  not_2 (.in_1(in_1), .out_2(not_2_out_2));
  g g_1 (.in_1(in_1), .out_3(g_1_out_3), .in_2(in_2));
  p p_1 (.out_3(p_1_out_3), .in_1(in_1), .in_2(in_2));
  \or  or_1 (.in_1(and_1_out_3), .in_2(and_2_out_3), .out_3(out_4));
  \and  and_3 (.in_1(p_1_out_3), .in_2(in_3), .out_3(and_3_out_3));
  \or  or_2 (.in_1(g_1_out_3), .in_2(and_3_out_3), .out_3(out_5));
endmodule

module full (
  input  in_1,
  input  in_2,
  input  in_3,
  input  in_4,
  input  in_5,
  input  in_6,
  input  in_7,
  output out_8,
  output out_9
);

  k0 k0_1 (.in_1(in_1), .in_2(in_4), .in_3(in_7), .out_4(out_8));  // open: out_5
  k1 k1_1 (.in_1(in_2), .in_2(in_5), .in_3(in_7), .out_4(out_9));  // open: out_5
endmodule
