// Logisim project flipflopsandlatches.circ as structural Verilog: 8 circuits, main circuit SR-LATCH
module SR_LATCH (
  input  ns,
  input  nr,
  output q,
  output nq
);

  nand n1 (q, ns, nq);
  nand n2 (nq, q, nr);

  // Notes on the sheet:
  //   SR Latch
endmodule

module D_FLIPFLOP (
  input  d,
  input  en,
  output q,
  output nq
);

  wire n1_out, n2_out;

  nand n1 (n1_out, d, en);
  nand n2 (n2_out, en, ~d);  // NAND_Gate
  SR_LATCH SR (.ns(n1_out), .nr(n2_out), .q(q), .nq(nq));

  // Notes on the sheet:
  //   D-FLIPFLOP
endmodule

module EDGE_SENSITIVE_D_FLIPFLOP (
  input  clk,
  input  data,
  output q
);

  wire n1_out, n2_out, S_nq;

  nand n1 (n1_out, S_nq, clk, n2_out);
  nand n2 (n2_out, n1_out, data);
  SR_LATCH S (.ns(n2_out), .nr(clk), .nq(S_nq));  // open: q
  SR_LATCH C (.ns(S_nq), .nr(n1_out), .q(q));  // open: nq

  // Notes on the sheet:
  //   EDGE-SENSITIVE-D-FLIPFLOP
  //   rising edge sensitive
endmodule

module CLOCKED_GATED_D_FLIPFLOP (
  input  clk,
  input  en,
  input  data,
  output Q
);

  wire A1_out, A2_out, SR1_nq, SR2_nq, SR2_q;

  and A1 (A1_out, en, clk);
  and A2 (A2_out, SR1_nq, en, clk);
  SR_LATCH SR1 (.ns(SR2_nq), .nr(A1_out), .nq(SR1_nq));  // open: q
  SR_LATCH SR2 (.ns(A2_out), .nr(data), .q(SR2_q), .nq(SR2_nq));
  SR_LATCH SRC (.ns(SR1_nq), .nr(SR2_q), .q(Q));  // open: nq

  // Notes on the sheet:
  //   CLOCKED-AND-GATED-D-FLIPFLOP
endmodule

module RESETABLE_CLK_GATE_D_FLIPFLOP (
  input  clk,
  input  en,
  input  data,
  input  reset,
  output Q
);

  wire A1_out, A2_out, A3_out, or_1_out, SR1_nq, SR2_nq, SR2_q;

  and A1 (A1_out, en, clk);
  and A2 (A2_out, SR1_nq, en, clk);
  SR_LATCH SR1 (.ns(SR2_nq), .nr(A1_out), .nq(SR1_nq));  // open: q
  SR_LATCH SR2 (.ns(A2_out), .nr(data), .q(SR2_q), .nq(SR2_nq));
  or or_1 (or_1_out, SR1_nq, ~reset);  // OR_Gate
  and A3 (A3_out, SR2_q, reset);
  SR_LATCH SRC (.ns(or_1_out), .nr(A3_out), .q(Q));  // open: nq

  // Notes on the sheet:
  //   RESETABLE-CLOCKED-AND-GATED-D-FLIPFLOP
endmodule

module _8_BIT_REGISTER (
  input  clk,
  input  [7:0] D,
  input  en,
  input  rst,
  output [7:0] out_5
);

  RESETABLE_CLK_GATE_D_FLIPFLOP BIT0 (.clk(clk), .en(en), .data(D[0]), .reset(rst), .Q(out_5[0]));
  RESETABLE_CLK_GATE_D_FLIPFLOP BIT2 (.clk(clk), .en(en), .data(D[2]), .reset(rst), .Q(out_5[2]));
  RESETABLE_CLK_GATE_D_FLIPFLOP BIT4 (.clk(clk), .en(en), .data(D[4]), .reset(rst), .Q(out_5[4]));
  RESETABLE_CLK_GATE_D_FLIPFLOP BIT6 (.clk(clk), .en(en), .data(D[6]), .reset(rst), .Q(out_5[6]));
  RESETABLE_CLK_GATE_D_FLIPFLOP BIT1 (.clk(clk), .en(en), .data(D[1]), .reset(rst), .Q(out_5[1]));
  RESETABLE_CLK_GATE_D_FLIPFLOP BIT3 (.clk(clk), .en(en), .data(D[3]), .reset(rst), .Q(out_5[3]));
  RESETABLE_CLK_GATE_D_FLIPFLOP BIT5 (.clk(clk), .en(en), .data(D[5]), .reset(rst), .Q(out_5[5]));
  RESETABLE_CLK_GATE_D_FLIPFLOP BIT7 (.clk(clk), .en(en), .data(D[7]), .reset(rst), .Q(out_5[7]));

  // Other names for the same wires on the sheet: q0 = out_5[0]; q1 = out_5[1]; q2 = out_5[2]; q3 = out_5[3];
  //   q4 = out_5[4]; q5 = out_5[5]; q6 = out_5[6]; q7 = out_5[7]

  // Notes on the sheet:
  //   enable reset to use
  //   8-BIT-REGISTER
endmodule

module incr (
  input  [7:0] in_1,
  input  in_2,
  output [7:0] out_3
);

  wire button_1_out, clock_1_out, not_1_out;
  wire [7:0] adder_1_out;

  Clock clock_1 (.out(clock_1_out));
  not not_1 (not_1_out, button_1_out);
  Button button_1 (.out(button_1_out));
  Adder adder_1 (.a(in_1), .b(out_3), .out(adder_1_out), .cin(1'b1));  // open: cout
  _8_BIT_REGISTER u_8_bit_register_1 (.clk(clock_1_out), .D(adder_1_out), .en(in_2), .rst(not_1_out), .out_5(out_3));
  Hex_Digit_Display hex_digit_display_1 (.value(out_3[7:4]), .dp(1'b0));
  Hex_Digit_Display hex_digit_display_2 (.value(out_3[3:0]), .dp(1'b0));
endmodule

module muxaddsubcmpreg (
  input  in_1,
  input  [7:0] in_2,
  input  [7:0] in_3,
  input  en,
  input  [1:0] in_5,
  input  in_6,
  input  in_7,
  output [7:0] out_8,
  output [7:0] out_9,
  output [7:0] out_10,
  output [7:0] out_11
);

  wire clock_1_out;
  wire [7:0] demultiplexer_1_out0, demultiplexer_1_out1, demultiplexer_1_out2, demultiplexer_1_out3,
       n8bitaddsubcmp_1_result;

  Clock clock_1 (.out(clock_1_out));
  Button button_1 ();  // open: out
  _8bitaddsubcmp u_8bitaddsubcmp_1 (
    .Add_Sub(in_1), .Operand_X(in_2), .Operand_Y(in_3), .in_4(1'b0), .Result(n8bitaddsubcmp_1_result));  // open: OA_Flag, L_flag, carry_borrow_out, O_flag
  Demultiplexer #(.select(2), .width(8)) demultiplexer_1 (
    .out0(demultiplexer_1_out0), .out1(demultiplexer_1_out1), .out2(demultiplexer_1_out2),
    .out3(demultiplexer_1_out3), .in(n8bitaddsubcmp_1_result), .sel(in_5), .en(en));
  _8_BIT_REGISTER u_8_bit_register_1 (
    .clk(clock_1_out), .D(demultiplexer_1_out0), .en(in_6), .rst(in_6), .out_5(out_8));
  _8_BIT_REGISTER u_8_bit_register_2 (
    .clk(clock_1_out), .D(demultiplexer_1_out1), .en(in_6), .rst(in_6), .out_5(out_9));
  _8_BIT_REGISTER u_8_bit_register_3 (
    .clk(clock_1_out), .D(demultiplexer_1_out2), .en(in_6), .rst(in_6), .out_5(out_10));
  _8_BIT_REGISTER u_8_bit_register_4 (
    .clk(clock_1_out), .D(demultiplexer_1_out3), .en(in_6), .rst(in_6), .out_5(out_11));

  assign in_7 = in_6;
endmodule
