// Logisim project gates.circ as structural Verilog: 7 circuits, main circuit nand
module \nand  (
  input  in_1,
  input  in_2,
  output out_3
);

  wire transistor_3_out;

  Transistor transistor_1 (.in(1'b1), .out(out_3), .gate(in_1));
  Transistor #(.\type ("n")) transistor_2 (.in(transistor_3_out), .out(out_3), .gate(in_1));
  Transistor #(.\type ("n")) transistor_3 (.in(1'b0), .out(transistor_3_out), .gate(in_2));
  Transistor #(.gate("br")) transistor_4 (.in(1'b1), .out(out_3), .gate(in_2));
endmodule

module \not  (
  input  in_1,
  output out_2
);

  \nand  nand_1 (.in_1(in_1), .in_2(in_1), .out_3(out_2));
endmodule

module \and  (
  input  in_1,
  input  in_2,
  output out_3
);

  wire nand_1_out_3;

  \nand  nand_1 (.in_1(in_1), .in_2(in_2), .out_3(nand_1_out_3));
  \nand  nand_2 (.in_1(nand_1_out_3), .in_2(nand_1_out_3), .out_3(out_3));
endmodule

module \or  (
  input  in_1,
  input  in_2,
  output out_3
);

  wire nand_1_out_3, nand_2_out_3;

  \nand  nand_1 (.in_1(in_1), .in_2(in_1), .out_3(nand_1_out_3));
  \nand  nand_2 (.in_1(in_2), .in_2(in_2), .out_3(nand_2_out_3));
  \nand  nand_3 (.in_1(nand_1_out_3), .in_2(nand_2_out_3), .out_3(out_3));
endmodule

module cond (
  input  in_1,
  input  in_2,
  output out_3
);

  wire not_1_out_2;

  \not  not_1 (.in_1(in_1), .out_2(not_1_out_2));
  \or  or_1 (.in_1(not_1_out_2), .in_2(in_2), .out_3(out_3));
endmodule

module \xor  (
  input  in_1,
  input  in_2,
  output out_3
);

  wire and_1_out_3, not_1_out_2, or_1_out_3;

  \or  or_1 (.in_1(in_1), .in_2(in_2), .out_3(or_1_out_3));
  \not  not_1 (.in_1(and_1_out_3), .out_2(not_1_out_2));
  \and  and_1 (.in_1(in_1), .in_2(in_2), .out_3(and_1_out_3));
  \and  and_2 (.in_1(or_1_out_3), .in_2(not_1_out_2), .out_3(out_3));
endmodule

module biconditional (
  input  in_1,
  input  in_2,
  output out_3
);

  wire cond_1_out_3, cond_2_out_3;

  cond cond_1 (.in_1(in_1), .in_2(in_2), .out_3(cond_1_out_3));
  cond cond_2 (.in_1(in_2), .in_2(in_1), .out_3(cond_2_out_3));
  \and  and_1 (.in_1(cond_1_out_3), .in_2(cond_2_out_3), .out_3(out_3));
endmodule
