// Logisim project nand2.circ as structural Verilog: 3 circuits, main circuit nand2
module nand2 (
  input  in_1,
  input  in_2,
  output out_3
);

  wire transistor_3_out;

  Transistor transistor_1 (.in(1'b1), .out(out_3), .gate(in_1));
  Transistor #(.\type ("n")) transistor_2 (.in(transistor_3_out), .out(out_3), .gate(in_1));
  Transistor #(.\type ("n")) transistor_3 (.in(1'b0), .out(transistor_3_out), .gate(in_2));
  Transistor #(.gate("br")) transistor_4 (.in(1'b1), .out(out_3), .gate(in_2));
endmodule

module Gate1 (
  input  in_1,
  output out_2
);

  nand2 nand2_1 (.in_1(in_1), .in_2(in_1), .out_3(out_2));
endmodule

module Gate2 (
  input  in_1,
  input  in_2,
  output out_3
);

  wire nand2_1_out_3;

  nand2 nand2_1 (.in_1(in_1), .in_2(in_2), .out_3(nand2_1_out_3));
  nand2 nand2_2 (.in_1(nand2_1_out_3), .in_2(nand2_1_out_3), .out_3(out_3));
endmodule
